# Fritzing sketch greenmilefritzing (saved by Fritzing 1.0.5)
circuit board: 6.5cm x 5.2cm
breadboards: 1

parts:
  SPS30 = IC, SIP package, 5 pins [chip_label=SPS30]
  LilyGo_ESP32S3_SIM7080G = LILYGO TTGO-T SIM7080G-S3
  KY_-_016 = KY-016 RGB Full Color LED Module [package="Breakout board"]
  SHT41 = Adafruit SHT4x [part_number="Adafruit #4885"]

nets (from the pcb view):
  N1: SPS30.pin1, LilyGo_ESP32S3_SIM7080G.pin_1, LilyGo_ESP32S3_SIM7080G.pin_36, SHT41.VCC
  N2: SPS30.pin2, LilyGo_ESP32S3_SIM7080G.pin_6, SHT41.SDA
  N3: SPS30.pin3, LilyGo_ESP32S3_SIM7080G.pin_9, SHT41.SCL
  N4: SPS30.pin4, SPS30.pin5, LilyGo_ESP32S3_SIM7080G.pin_15, LilyGo_ESP32S3_SIM7080G.pin_22, KY_-_016.-, SHT41.GND
  N5: LilyGo_ESP32S3_SIM7080G.pin_28, KY_-_016.B
  N6: LilyGo_ESP32S3_SIM7080G.pin_29, KY_-_016.G
  N7: LilyGo_ESP32S3_SIM7080G.pin_30, KY_-_016.R

notes:
  LilyGo ESP32S3 SIM7080G
  SPS30
  SHT41
  KY -016
  VCC
  GND
  SCL
  SDA
  SEL
  VDD
  GRND - G - B - R
  3V3
  GRD
  GPIO8
  GPIO9
  GPIO 35 -36 -37

custom parts:
  LILYGO TTGO-T SIM7080G-S3: The SIM7080G is Multi-Band CAT-M and NB-IoT module solution in a SMT type .
  KY-016 RGB Full Color LED Module: KY-016 Arduino full color 5mm RGB LED, different colors can be obtained by mixing the three primary colors.
  Adafruit SHT4x: Sensirion Temperature/Humidity sensors are some of the finest & highest-accuracy devices you can get. And finally, we have some that have a true I2C interface for easy reading. The SHT40 and SHT45 sensors are the fourth generation (started at the SHT10 and worked its way up to the top!). The SHT40 has an excellent ±1.8% typical relative humidity accuracy from 25 to 75% and ±0.2 °C typical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
